# Fritzing sketch Fans_With_Arduino (saved by Fritzing 0.9.3b)
breadboards: 1

parts:
  Εξάρτημα1 = Arduino Nano (Rev3.0) (ICSP)
  JP1 = Header 4 [package=screwterminal-3.5mm-4_lock]
  JP2 = Header 3 [package=screwterminal-3.5mm-3_lock.007s]
  R1 = Resistor [tolerance=±5% resistance=220 package="0805 [SMD]"]

nets:
  N1: Εξάρτημα1.D2, JP1.3, R1.Pin_1
  N2: Εξάρτημα1.D9, JP1.4
  N3: Εξάρτημα1.VIN, R1.Pin_0
  N4: Εξάρτημα1.GND, JP1.2, JP2.2
  N5: JP1.1, JP2.1

notes:
  PWR_SUPPLY
  FAN
  10k
