# Fritzing sketch Indoors (saved by Fritzing 0.9.3b)
breadboards: 1

parts:
  MCU1 = Raspberry Pi Zero  # not connected
  Εξάρτημα2 = Arduino Nano (Rev3.0) (ICSP)
  MQ7 = MQ-7 breakout
  MQ4 = MQ-4
  PMSA003I = Adafruit PMSA003I Air Quality Breakout [part_number=0x12]
  J1 = Power Jack [package=power_jack_pth_lock]
  MQ2 = GAS_SENSOR [package=mq-3]  # not connected
  MQ131 = MQ-4
  MQ137 = MQ-4
  BME680 = Adafruit BME680 [part_number=0x76]
  SGP40 = Adafruit SGP40 [part_number=0x59]

nets:
  N1: Εξάρτημα2.D6, MQ131.DO
  N2: Εξάρτημα2.D7, MQ137.DO
  N3: Εξάρτημα2.D8, MQ7.DO
  N4: Εξάρτημα2.D9, MQ4.DO
  N5: Εξάρτημα2.A7, MQ137.AO
  N6: Εξάρτημα2.A6, MQ131.AO
  N7: Εξάρτημα2.A5, PMSA003I.SCL, BME680.SCK/SCL, SGP40.SCL
  N8: Εξάρτημα2.A4, PMSA003I.SDA, BME680.SDI/SDA, SGP40.SDA
  N9: Εξάρτημα2.A3, MQ7.AO
  N10: Εξάρτημα2.A2, MQ4.AO
  VCC: MQ7.VCC, MQ4.VCC, PMSA003I.VCC, J1.PWR, MQ131.VCC, MQ137.VCC, BME680.VCC, SGP40.VCC
  GND: MQ7.GND, MQ4.GND, PMSA003I.GND, J1.GND, MQ131.GND, MQ137.GND, BME680.GND, SGP40.GND

custom parts:
  MQ-7 breakout: MQ-5 gas sensor
  Adafruit PMSA003I Air Quality Breakout: Breathe easy, knowing that you can track and sense the quality of the air around you with this Adafruit PMSA003I Air Quality Breakout. This sensor is great for monitoring air quality, in a compact plug-in format. Best of all, unlike almost all other sensors we've seen that are UART interface, this one is I2C interface, which makes it a great match for single board Linux computers like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
