# Fritzing sketch Outdoors (saved by Fritzing 0.9.3b)
breadboards: 1

parts:
  MCU1 = Raspberry Pi Zero  # not connected
  Εξάρτημα2 = Arduino Nano (Rev3.0) (ICSP)
  MCP9808 = MCP9808 [part_number=0x18]
  BMP180 = Barometric Pressure Sensor - BMP180 Breakout (GY-68) [part_number=0x77]
  MQ7 = MQ-7 breakout
  MQ4 = MQ-4
  PMSA003I = Adafruit PMSA003I Air Quality Breakout [part_number=0x12]
  J1 = Power Jack [package=power_jack_pth_lock]
  MQ2 = GAS_SENSOR [package=mq-3]  # not connected

nets:
  N1: Εξάρτημα2.D8, MQ7.DO
  N2: Εξάρτημα2.D9, MQ4.DO
  N3: Εξάρτημα2.A5, MCP9808.SCL, BMP180.SCL, PMSA003I.SCL
  N4: Εξάρτημα2.A4, MCP9808.SDA, BMP180.SDA, PMSA003I.SDA
  N5: Εξάρτημα2.A3, MQ7.AO
  N6: Εξάρτημα2.A2, MQ4.AO
  VCC: MCP9808.VCC, BMP180.VCC, MQ7.VCC, MQ4.VCC, PMSA003I.VCC, J1.PWR
  GND: MCP9808.GND, BMP180.GND, MQ7.GND, MQ4.GND, PMSA003I.GND, J1.GND

custom parts:
  MQ-7 breakout: MQ-5 gas sensor
  Adafruit PMSA003I Air Quality Breakout: Breathe easy, knowing that you can track and sense the quality of the air around you with this Adafruit PMSA003I Air Quality Breakout. This sensor is great for monitoring air quality, in a compact plug-in format. Best of all, unlike almost all other sensors we've seen that are UART interface, this one is I2C interface, which makes it a great match for single board Linux computers like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
